# Fritzing sketch simple (saved by Fritzing 0.8.5b)
breadboards: 1

parts:
  Raspberry_Pi_B_rev1 = Raspberry Pi B rev2  # not connected
  Power_plug1 = Power plug
  Part1 = Thermal Printer

nets:
  N1: Power_plug1.VCC, Part1.VH
  N2: Power_plug1.GND, Part1.GND#0
